# Fritzing sketch photon-boardroom-beacon-pcb (saved by Fritzing 0.9.3b)
circuit board: 8.46667cm x 5.64444cm
breadboards: 2
perfboards: 3

parts:
  Part1 = Photon
  LED1 = RGB LED (com. cathode, rgb) [part_number=LEDMU-999299 package="5 mm [THT]"]
  LED2 = RGB LED (com. cathode, rgb) [part_number=LEDMU-999299 package="5 mm [THT]"]
  LED3 = RGB LED (com. cathode, rgb) [part_number=LEDMU-999299 package="5 mm [THT]"]
  R1 = Resistor [tolerance=±5% resistance=1k package="2010 [SMD]"]
  R2 = Resistor [tolerance=±5% resistance=1k package="2010 [SMD]"]
  R3 = Resistor [tolerance=±5% resistance=1k package="2010 [SMD]"]
  R4 = Resistor [tolerance=±5% resistance=1k package="2010 [SMD]"]
  R5 = Resistor [tolerance=±5% resistance=1k package="2010 [SMD]"]
  R6 = Resistor [tolerance=±5% resistance=1k package="2010 [SMD]"]
  R7 = Resistor [tolerance=±5% resistance=1k package="2010 [SMD]"]
  R8 = Resistor [tolerance=±5% resistance=1k package="2010 [SMD]"]
  R9 = Resistor [tolerance=±5% resistance=1k package="2010 [SMD]"]
  Part2 = PowerBoost 500 Charger
  U1 = LIPO-1000mAh [package=lipo-1000]
  PIR1 = PIR sensor
  LED4 = LEDs [package=led10mm]
  R10 = Resistor [tolerance=±5% resistance=220 package="1206 [SMD]"]
  Part3 = Photon  # not connected
  LED5 = RGB LED (com. cathode, rgb) [part_number=LEDMU-999299 package="5 mm [THT]"]  # not connected
  LED6 = RGB LED (com. cathode, rgb) [part_number=LEDMU-999299 package="5 mm [THT]"]  # not connected
  LED7 = RGB LED (com. cathode, rgb) [part_number=LEDMU-999299 package="5 mm [THT]"]  # not connected
  LED8 = RGB LED (com. cathode, rgb) [part_number=LEDMU-999299 package="5 mm [THT]"]  # not connected
  LED10 = RGB LED (com. cathode, rgb) [part_number=LEDMU-999299 package="5 mm [THT]"]  # not connected

nets (from the breadboard view):
  N1: Part1.A0, LED2.red_anode, R9.Pin_0, R9.Pin_1
  N2: Part1.A1, LED2.common_cathode, R8.Pin_0, R8.Pin_1
  N3: Part1.A2, LED2.blue_anode, R5.Pin_0, R5.Pin_1
  GND: Part1.GND, LED1.green_anode, LED2.green_anode, LED3.green_anode, PIR1.GND, R10.Pin_1
  VIN: Part1.VIN, PIR1.VDD
  N4: Part1.D0, LED1.blue_anode, R4.Pin_0, R4.Pin_1
  N5: Part1.D1, LED1.common_cathode, R6.Pin_0, R6.Pin_1
  N6: Part1.D2, LED1.red_anode, R7.Pin_0, R7.Pin_1
  N7: Part1.D3, LED3.blue_anode, R3.Pin_0, R3.Pin_1
  N8: Part1.D4, LED3.common_cathode, R2.Pin_0, R2.Pin_1
  N9: Part1.D5, LED3.red_anode, R1.Pin_0, R1.Pin_1
  N10: Part1.D6, PIR1.SIG
  N11: Part1.D7, LED4.C
  N12: Part2.GND_BAT_IN, U1.-
  N13: Part2.VBAT_IN, U1.+
  N14: LED4.A, R10.Pin_0

notes:
  RGB 10mm (x3)
  CC Diffuse
  3/3.2V 20mA
  LEDMU-999299
  1K Resistor (x9)
  PIR MOTION SENSORSPEDE-028101
  Input Voltage: 4.5 to 20V Output Signal: 0.3 to 5V Maximum Distance: 7M Sensing Angle: 110 Degree
  CAUTION: Positive and Negative should be opposite to this diagram for the SENSORSPEDE-028101
  LED
  220ohm resistor
  5V USB POWERBOOST 1000 LIPOLY CHARGER & BOOSTER
  BATCC-912110
  Led 1: D2, D1, D0
  Led 2: D3, D4, D5
  Led 3: A0, A1, A2
  PIR Input: D6
  PIR Status: D7
  PIR Power: VIN
